// Logisim project CS441_SamG_Homework1.circ as structural Verilog: 1 circuit, main circuit main
module main (
);

  wire clock_1_out, comparator_1_gt, undriven;
  wire [3:0] A_q, adder_1_out, adder_2_out, B_q, divider_1_out, multiplexer_1_out, multiplexer_2_out,
       multiplexer_3_out, multiplier_1_out, register_1_q, subtractor_1_out;
  wire [6:0] ram_1_data;

  Clock clock_1 (.out(clock_1_out));
  Multiplexer #(.width(4), .enable("false")) multiplexer_1 (
    .in0(multiplexer_3_out), .in1(4'b0000), .out(multiplexer_1_out), .sel(ram_1_data[5]));
  Register #(.width(4)) register_1 (.D(multiplexer_2_out), .Q(register_1_q), .clk(clock_1_out));  // open: en, clr
  Multiplexer #(.width(4), .enable("false")) multiplexer_2 (
    .in0(adder_1_out), .in1(4'b0000), .out(multiplexer_2_out), .sel(comparator_1_gt));
  Register #(.width(4)) A (.D(multiplexer_1_out), .Q(A_q), .clk(clock_1_out));  // open: en, clr
  Adder #(.width(4)) adder_1 (.a(register_1_q), .b(4'b0001), .out(adder_1_out));  // open: cin, cout
  Comparator #(.width(4), .mode("unsigned")) comparator_1 (
    .a(4'b1111), .b(adder_2_out), .gt(comparator_1_gt));  // open: eq, lt
  Counter #(.width(4), .max('h5)) B (
    .load(undriven), .D(4'b0000), .Q(B_q), .clk(clock_1_out), .clr(ram_1_data[6]));  // open: count, carry
  Hex_Digit_Display hex_digit_display_1 (.value(multiplexer_3_out));  // open: dp
  RAM #(.addrWidth(4), .dataWidth(7)) ram_1 (.addr(register_1_q), .data(ram_1_data));  // open: sel, clk, ld, clr
  Adder #(.width(4)) adder_2 (.a(A_q), .b(B_q), .out(adder_2_out));  // open: cin, cout
  Subtractor #(.width(4)) subtractor_1 (.a(A_q), .b(B_q), .out(subtractor_1_out));  // open: bin, bout
  Multiplier #(.width(4)) multiplier_1 (.a(A_q), .b(B_q), .out(multiplier_1_out));  // open: cin, cout
  Divider #(.width(4)) divider_1 (.a(A_q), .b(B_q), .out(divider_1_out));  // open: upper, rem
  Multiplexer #(.select(2), .width(4), .enable("false")) multiplexer_3 (
    .in0(adder_2_out), .in1(subtractor_1_out), .in2(multiplier_1_out), .in3(divider_1_out),
    .out(multiplexer_3_out), .sel(ram_1_data[1:0]));

  // Notes on the sheet:
  //   Registers
  //   Program Counter
  //   Instruction Set
  //   ALU
  //   Output
endmodule
